# Fritzing sketch ledstrip (saved by Fritzing 0.9.2b)
breadboards: 1

parts:
  Bauteil1 = Arduino Nano (Rev3.0)
  Bauteil2 = ENC28J60 Breakout Board
  Q1 = TIP120 Hi-Current Darlington Transistor
  Q2 = TIP120 Hi-Current Darlington Transistor
  Q3 = TIP120 Hi-Current Darlington Transistor  # not connected
  R1 = Resistor [tolerance=±5% resistance=220 package=THT]  # not connected
  R2 = Resistor [tolerance=±5% resistance=220 package=THT]  # not connected
  R3 = Resistor [tolerance=±5% resistance=220 package=THT]  # not connected

nets:
  N1: Bauteil1.D2, Q2.EMITTER
  N2: Bauteil1.D3, Q2.COLLECTOR
  N3: Bauteil1.D4, Q2.BASE
  N4: Bauteil1.D7, Q1.EMITTER
  N5: Bauteil1.D8, Q1.COLLECTOR
  N6: Bauteil1.D9, Q1.BASE
  3V3: Bauteil1.3V3, Bauteil2.VCC

custom parts:
  ENC28J60 Breakout Board: This is a breakout board for the Microchip ENC28J60 stand-alone ethernet controller. The ENC28J60 has an SPI interface. It operates at 3.3 Volts.
